// Digital circuit implementação circuito , grupo 17 , Diogo Silva e Ahmed Al-Majmaie.dig as structural Verilog
module implementac_a_o_circuito___grupo_17___Diogo_Silva_e_Ahmed_Al_Majmaie (
  input  clk
);

  wire a_dezenas_e_b_unidades_eq, a_unidades_b_dezenas_eq, and_1_out, and_2_out, and_3_out, and_4_out,
       button_1_out, button_2_out, button_3_out, button_4_out, comparador_dezenas_eq, comparador_unidades_eq,
       counter_5_ovf, d_ff_1_nq, d_ff_1_q, d_ff_as_1_nq, d_ff_as_2_nq, delete_2_out, delete_out,
       jogador1_out, jogador_2_out, multiplexer_4_out, multiplexer_5_out, nor_1_out, or_1_out, or_2_out,
       or_3_out, or_4_out, or_5_out, or_6_out, reset_2_out, reset_out, ronda;
  wire [3:0] counter_1_out, counter_2_out, counter_3_out, counter_4_out, counter_5_out, counter_6_out,
       j1_dez, j1_uni, j2_dez, j2_uni, multiplexer_1_out, multiplexer_2_out, multiplexer_3_out,
       multiplexer_6_out;

  Button delete (.out(delete_out));
  Button delete_2 (.out(delete_2_out));
  or or_1 (or_1_out, and_3_out, delete_out);
  Button button_1 (.out(button_1_out));
  Button reset (.out(reset_out));
  or or_2 (or_2_out, and_4_out, delete_2_out);
  or or_3 (or_3_out, delete_2_out, and_1_out);
  Button button_2 (.out(button_2_out));
  or or_4 (or_4_out, delete_out, and_2_out);
  Button jogador1 (.out(jogador1_out));
  and and_1 (and_1_out, button_2_out, d_ff_as_1_nq);
  Button jogador_2 (.out(jogador_2_out));
  and and_2 (and_2_out, button_1_out, d_ff_as_2_nq);
  D_FF_AS d_ff_as_1 (.Set(1'b0), .D(1'b1), .C(jogador1_out), .Clr(reset_out), .nQ(d_ff_as_1_nq));  // open: Q
  Button button_3 (.out(button_3_out));
  Button button_4 (.out(button_4_out));
  and and_3 (and_3_out, button_3_out, d_ff_as_2_nq);
  Register #(.Bits(4)) register_1 (.D(counter_1_out), .C(jogador1_out), .en(1'b1), .Q(j1_uni));
  Counter #(.Bits(4)) counter_1 (.en(1'b1), .C(or_2_out), .clr(delete_2_out), .out(counter_1_out));  // open: ovf
  Counter #(.Bits(4)) counter_2 (.en(1'b1), .C(or_3_out), .clr(delete_2_out), .out(counter_2_out));  // open: ovf
  Register #(.Bits(4)) register_2 (.D(counter_2_out), .C(jogador1_out), .en(1'b1), .Q(j1_dez));
  D_FF_AS d_ff_as_2 (.Set(1'b0), .D(1'b1), .C(jogador_2_out), .Clr(reset_2_out), .nQ(d_ff_as_2_nq));  // open: Q
  Register #(.Bits(4)) register_3 (.D(counter_3_out), .C(jogador_2_out), .en(1'b1), .Q(j2_uni));
  Counter #(.Bits(4)) counter_3 (.en(1'b1), .C(or_1_out), .clr(delete_out), .out(counter_3_out));  // open: ovf
  Counter #(.Bits(4)) counter_4 (.en(1'b1), .C(or_4_out), .clr(delete_out), .out(counter_4_out));  // open: ovf
  Register #(.Bits(4)) register_4 (.D(counter_4_out), .C(jogador_2_out), .en(1'b1), .Q(j2_dez));
  and and_4 (and_4_out, button_4_out, d_ff_as_1_nq);
  or or_5 (or_5_out, jogador_2_out, jogador_2_out);
  or or_6 (or_6_out, reset_2_out, reset_out);
  Seven_Seg_Hex seven_seg_hex_1 (.d(counter_2_out), .dp(1'b0));
  Button reset_2 (.out(reset_2_out));
  Seven_Seg_Hex seven_seg_hex_2 (.d(counter_4_out), .dp(1'b0));
  Seven_Seg_Hex seven_seg_hex_3 (.d(counter_1_out), .dp(1'b0));
  Seven_Seg_Hex seven_seg_hex_4 (.d(counter_3_out), .dp(1'b0));
  Counter #(.Bits(4)) counter_5 (.en(1'b1), .C(or_5_out), .clr(or_6_out), .out(counter_5_out), .ovf(counter_5_ovf));
  Counter #(.Bits(4)) counter_6 (.en(1'b1), .C(counter_5_ovf), .clr(or_6_out), .out(counter_6_out));  // open: ovf
  Comparator #(.Bits(4)) a_unidades_b_dezenas (
    .a(multiplexer_2_out), .b(multiplexer_3_out), .eq(a_unidades_b_dezenas_eq));  // open: gt, lt
  Comparator #(.Bits(4)) comparador_unidades (
    .a(multiplexer_2_out), .b(multiplexer_6_out), .eq(comparador_unidades_eq));  // open: gt, lt
  Comparator #(.Bits(4)) comparador_dezenas (
    .a(multiplexer_1_out), .b(multiplexer_3_out), .eq(comparador_dezenas_eq));  // open: gt, lt
  Comparator #(.Bits(4)) a_dezenas_e_b_unidades (
    .a(multiplexer_1_out), .b(multiplexer_6_out), .eq(a_dezenas_e_b_unidades_eq));  // open: gt, lt
  Seven_Seg_Hex seven_seg_hex_5 (.d(counter_6_out), .dp(1'b0));
  Seven_Seg_Hex seven_seg_hex_6 (.d(counter_5_out), .dp(1'b0));
  DipSwitch seletor_ronda (.out(ronda));
  Multiplexer #(.Bits(4)) multiplexer_1 (.sel(ronda), .in_0(j1_dez), .in_1(j2_dez), .out(multiplexer_1_out));
  Multiplexer #(.Bits(4)) multiplexer_2 (.sel(ronda), .in_0(j1_uni), .in_1(j2_uni), .out(multiplexer_2_out));
  Multiplexer #(.Bits(4)) multiplexer_3 (.sel(ronda), .in_0(j2_dez), .in_1(j1_dez), .out(multiplexer_3_out));
  Multiplexer multiplexer_4 (
    .sel(d_ff_1_q), .in_0(comparador_unidades_eq), .in_1(comparador_dezenas_eq), .out(multiplexer_4_out));
  Multiplexer multiplexer_5 (
    .sel(d_ff_1_q), .in_0(a_unidades_b_dezenas_eq), .in_1(a_dezenas_e_b_unidades_eq), .out(multiplexer_5_out));
  Multiplexer #(.Bits(4)) multiplexer_6 (.sel(ronda), .in_0(j2_uni), .in_1(j1_uni), .out(multiplexer_6_out));
  D_FF d_ff_1 (.D(d_ff_1_nq), .C(clk), .Q(d_ff_1_q), .nQ(d_ff_1_nq));
  LED led_1 (.in(multiplexer_5_out));
  LED led_2 (.in(multiplexer_4_out));
  nor nor_1 (nor_1_out, multiplexer_4_out, multiplexer_5_out);
  LED led_3 (.in(nor_1_out));

  // Notes on the sheet:
  //   contador de tentativas
  //   MUX_DezMestre
  //   MUX_UniMestre
  //   MUX_DezAdivinho
  //   MUX_UniAdivinho
endmodule
